# Fritzing sketch Output timers sketch (saved by Fritzing 1.0.5)
breadboards: 1

parts:
  J1 = STM32 Nucleo boards
  LED1 = smd LED [color="Blue (470nm)" package="0603 [SMD]"]
  R1 = Resistor [tolerance=±5% resistance=220 package="2512 [SMD]"]  # not connected
  M1 = Dagu DGServo 9g (Pan and tilt) [part_number=RS001B]

nets:
  N1: J1.GND#333, M1.gnd
  N2: J1.D10_PWM/SS, LED1.anode
  N3: J1.D11_PWM/MOSI, M1.pulse
  5V: J1.5V, M1.vcc
